# Fritzing sketch schematics (saved by Fritzing 0.9.3b)
breadboards: 1

parts:
  LCD1 = LCD screen
  Part1 = Arduino Uno (Rev3) - ICSP
  R1 = Resistor [tolerance=±5% resistance=220 package="0603 [SMD]"]
  R2 = Trimmer Potentiometer [maximum_resistance=10kΩ package=THT]
  S1 = Pushbutton [package="[THT]"]
  S2 = Pushbutton [package="[THT]"]
  R3 = Resistor [tolerance=±5% resistance=10k package=THT]
  R4 = Resistor [tolerance=±5% resistance=10k package=THT]
  S3 = Pushbutton [package="[THT]"]
  S4 = Pushbutton [package="[THT]"]
  S5 = Pushbutton [package="[THT]"]
  S6 = Pushbutton [package="[THT]"]
  S7 = Pushbutton [package="[THT]"]
  S8 = Pushbutton [package="[THT]"]
  R5 = Resistor [tolerance=±5% resistance=2.2k package=THT]
  R6 = Resistor [tolerance=±5% resistance=1k package=THT]
  R7 = Resistor [tolerance=±5% resistance=330 package=THT]
  R8 = Resistor [tolerance=±5% resistance=3.3k package=THT]
  R9 = Resistor [tolerance=±5% resistance=680 package=THT]
  J1 = Piezo Speaker

nets:
  VSS: LCD1.VSS, LCD1.R/W, LCD1.LED-, Part1.GND, R2.leg2, R3.Pin_1, R4.Pin_1, S3.Pin_3, S3.Pin_4, S4.Pin_3, S4.Pin_4, S5.Pin_3, S5.Pin_4, S6.Pin_3, S6.Pin_4, S7.Pin_3, S7.Pin_4, S8.Pin_3, S8.Pin_4, J1.pin1
  VDD: LCD1.VDD, Part1.5V, R1.Pin_0, R2.leg1, S1.Pin_3, S1.Pin_4, S2.Pin_1, S2.Pin_2, R5.Pin_0
  N1: LCD1.V0, R2.wiper
  N2: LCD1.RS, Part1.D12/MISO
  N3: LCD1.E, Part1.ICSP_MOSI, Part1.D11_PWM/MOSI
  N4: LCD1.DB4, Part1.D5_PWM
  N5: LCD1.DB5, Part1.D4
  N6: LCD1.DB6, Part1.D3_PWM
  N7: LCD1.DB7, Part1.D2
  N8: LCD1.LED+, R1.Pin_1
  N9: Part1.A0, S6.Pin_1, S6.Pin_2, R5.Pin_1, R7.Pin_1
  N10: Part1.D8, S1.Pin_1, S1.Pin_2, R3.Pin_0
  N11: Part1.D9_PWM, S2.Pin_3, S2.Pin_4, R4.Pin_0
  N12: Part1.D10_PWM/SS, J1.pin2
  N13: Part1.RESET, S8.Pin_1, S8.Pin_2
  N14: S3.Pin_1, S3.Pin_2, R6.Pin_0, R8.Pin_0
  N15: S4.Pin_1, S4.Pin_2, R6.Pin_1, R9.Pin_1
  N16: S5.Pin_1, S5.Pin_2, R7.Pin_0, R9.Pin_0
  N17: S7.Pin_1, S7.Pin_2, R8.Pin_1
